# Fritzing sketch theremin (saved by Fritzing 0.9.1b)
breadboards: 1

parts:
  Part1 = Arduino Uno (Rev3)
  R1 = Resistor [tolerance=±5% resistance=10k package=THT]
  R2 = Photocell (LDR) [package=THT]
  R3 = Rotary Potentiometer (Small) [maximum_resistance=10kΩ package=THT]
  J1 = Piezo Speaker
  R4 = Resistor [tolerance=±5% resistance=220 package=THT]
  R5 = Resistor [tolerance=±5% resistance=220 package=THT]
  R6 = Resistor [tolerance=±5% resistance=220 package=THT]
  SPKR1 = Loudspeaker

nets:
  N1: Part1.A0, R1.Pin_1, R2.pin_1
  N2: Part1.D8, R4.Pin_0, R5.Pin_0, R6.Pin_0
  N3: Part1.GND, R2.pin_0, R3.leg2, J1.pin1, SPKR1.pin1
  N4: Part1.D6_PWM, J1.pin2
  N5: Part1.5V, R1.Pin_0, R3.leg1
  N6: R4.Pin_1, R5.Pin_1, R6.Pin_1, SPKR1.pin2

// code stored in the sketch: theremin.ino
#define DEBUG (0)

//  ?????? ?? ???? ? ?????
const int ldr_pin = A0;  // ??????? ?? ??? ??? ? ??????? ???????
const int piezo_pin = 6;

// ??????????, ?????????? ? ??????????
int ldr_val = 0;        // ????????? ?????????? ???????? ?? ???????
int piezo_freg = 0;

// calibration vars
int cmin = 1023;
int cmax = 0;

void calibrate () {

    int tmp = 0;

    for (int i=0; i < 100; i++) {
        tmp = analogRead(ldr_pin);
        if (tmp > cmax) {
            cmax = tmp;
        }
        if (tmp < cmin) {
            cmin = tmp;
        }
        delay(10);
    }

}

void setup() {
#if DEBUG
    Serial.begin(9600);
    Serial.print("setup");
#endif

    pinMode(ldr_pin, INPUT);
    pinMode(piezo_pin, OUTPUT);

    calibrate();
}

void loop() {

    ldr_val = analogRead(ldr_pin);

    if (ldr_val < cmin-5) {
        piezo_freg     = map(ldr_val, 0, cmax, 1100, 6830);

#if DEBUG
        Serial.print("Num: ");
        Serial.print(led_brightness);
        Serial.print("\n");
        delay(30);
#endif

        // and now the music!
        digitalWrite(piezo_pin, HIGH);
        delayMicroseconds(piezo_freg / 2);

       // DOWN
       digitalWrite(piezo_pin, LOW);
       delayMicroseconds(piezo_freg / 2);
    }

}
